# Fritzing sketch voltimetro (saved by Fritzing 0.9.3b)
breadboards: 1

parts:
  PSU1 = Adjustable Breadboard Power Supply
  Voltmeter_(DC)1 = Multimeter (DC Voltage)
  VCC1 = Battery
  VCC2 = Battery block 9V
  U1 = BATTERY-2 [package=battery-aa]
  Voltmeter_(DC)2 = Multimeter (DC Voltage)
  Voltmeter_(DC)3 = Multimeter (DC Voltage)
  Voltmeter_(DC)4 = Multimeter (DC Voltage)

nets:
  N1: PSU1.Vout+, Voltmeter_(DC)1.V_Probe
  N2: PSU1.Vout-, Voltmeter_(DC)1.COM_Probe
  N3: VCC1.-, Voltmeter_(DC)3.COM_Probe
  N4: VCC1.+, Voltmeter_(DC)3.V_Probe
  N5: VCC2.-, Voltmeter_(DC)4.COM_Probe
  N6: U1.-1, Voltmeter_(DC)2.COM_Probe
  N7: U1.+1, Voltmeter_(DC)2.V_Probe

notes:
  Fuente

custom parts:
  Multimeter (DC Voltage): A standard multimeter to measure volatages, currents and resistances
