# Fritzing sketch voltimetro_2 (saved by Fritzing 0.9.3b)
breadboards: 1

parts:
  PSU1 = Adjustable Breadboard Power Supply
  Voltmeter_(DC)1 = Multimeter (DC Voltage)
  R1 = Resistor [tolerance=±5% resistance=220 package=THT]
  R2 = Resistor [tolerance=±5% resistance=220 package=THT]
  R3 = Resistor [tolerance=±5% resistance=220 package=THT]

nets:
  N1: PSU1.Vout+, R2.Pin_1
  N2: PSU1.Vout-, R1.Pin_0
  N3: Voltmeter_(DC)1.COM_Probe, R1.Pin_1, R3.Pin_0
  N4: Voltmeter_(DC)1.V_Probe, R3.Pin_1

notes:
  Fuente

custom parts:
  Multimeter (DC Voltage): A standard multimeter to measure volatages, currents and resistances
