# Fritzing sketch puente_diodos (saved by Fritzing 0.9.3b)
breadboards: 1

parts:
  LTR_1 = Monacor line transformer [part_number=LTR-110]
  Voltmeter_(DC)1 = Multimeter (DC Voltage)
  D1 = Rectifier Diode [part_number=1N4001 package="300 mil [THT]"]  # not connected
  D2 = Rectifier Diode [part_number=1N4001 package="300 mil [THT]"]

nets:
  N1: LTR_1.05, D2.anode
  N2: LTR_1.GND, Voltmeter_(DC)1.COM_Probe
  N3: Voltmeter_(DC)1.V_Probe, D2.cathode

custom parts:
  Multimeter (DC Voltage): A standard multimeter to measure volatages, currents and resistances
