# Fritzing sketch mide_pots (saved by Fritzing 0.9.3b)

parts:
  R2 = Rotary Potentiometer (Large) [maximum_resistance=100kΩ package=THT]
  Voltmeter_(DC)1 = Multimeter (DC Voltage)

nets:
  N1: R2.leg1, Voltmeter_(DC)1.V_Probe
  N2: R2.wiper, Voltmeter_(DC)1.COM_Probe

custom parts:
  Multimeter (DC Voltage): A standard multimeter to measure volatages, currents and resistances
