# Fritzing sketch mide_pot (saved by Fritzing 0.9.3b)

parts:
  Voltmeter_(DC)1 = Multimeter (DC Voltage)
  R1 = Trimmer Potentiometer [maximum_resistance=10kΩ package=THT]
  Voltmeter_(DC)2 = Multimeter (DC Voltage)
  U1 = POT [package=pot_alpha_rv16af-20]

nets:
  N1: Voltmeter_(DC)1.COM_Probe, R1.leg1
  N2: Voltmeter_(DC)1.V_Probe, R1.leg2
  N3: Voltmeter_(DC)2.COM_Probe, U1.A
  N4: Voltmeter_(DC)2.V_Probe, U1.E

custom parts:
  Multimeter (DC Voltage): A standard multimeter to measure volatages, currents and resistances
