# Fritzing sketch mide_prest (saved by Fritzing 0.9.3b)

parts:
  Voltmeter_(DC)1 = Multimeter (DC Voltage)
  R1 = Trimmer Potentiometer [maximum_resistance=10kΩ package=THT]

nets:
  N1: Voltmeter_(DC)1.COM_Probe, R1.wiper
  N2: Voltmeter_(DC)1.V_Probe, R1.leg2

custom parts:
  Multimeter (DC Voltage): A standard multimeter to measure volatages, currents and resistances
