# Fritzing sketch mide_res (saved by Fritzing 0.9.3b)
breadboards: 1

parts:
  Voltmeter_(DC)1 = Multimeter (DC Voltage)
  R1 = Resistor [tolerance=±5% resistance=220 package=THT]
  R2 = Resistor [tolerance=±5% resistance=100 package=THT]  # not connected
  R3 = Resistor [tolerance=±5% resistance=15k package=THT]  # not connected

nets:
  N1: Voltmeter_(DC)1.COM_Probe, R1.Pin_0
  N2: Voltmeter_(DC)1.V_Probe, R1.Pin_1

custom parts:
  Multimeter (DC Voltage): A standard multimeter to measure volatages, currents and resistances
