# Fritzing sketch pots (saved by Fritzing 0.9.3b)
breadboards: 1

parts:
  R1 = Rotary Potentiometer (Small) [maximum_resistance=100kΩ package=THT]  # not connected
  R2 = Rotary Potentiometer (Large) [maximum_resistance=100kΩ package=THT]
  R3 = Trimmer Potentiometer [maximum_resistance=10kΩ package=THT]  # not connected
  R4 = TRIMPOT [package=trim_pot_pth]  # not connected
  R5 = TRIMPOT [package=3362u-2]  # not connected
  Voltmeter_(DC)1 = Multimeter (DC Voltage)

nets:
  N1: R2.leg1, Voltmeter_(DC)1.V_Probe
  N2: R2.wiper, Voltmeter_(DC)1.COM_Probe

custom parts:
  Multimeter (DC Voltage): A standard multimeter to measure volatages, currents and resistances
